// Logisim project Basic-16-bit-CPU.circ as structural Verilog
module _16_bit_ALU (
  input  [15:0] A,
  input  [15:0] B,
  input  [2:0] ALU_Op,
  output Zero,
  output [15:0] ALU_Out
);

  wire and_1_out, not_2_out;
  wire [15:0] adder_1_out, and_2_out, multiplexer_1_out, not_1_out, or_1_out;

  Multiplexer #(.width(16), .enable("false")) multiplexer_1 (
    .in0(B), .in1(not_1_out), .out(multiplexer_1_out), .sel(and_1_out));
  assign not_1_out = ~B;  // NOT_Gate not_1, 16 bits wide
  and and_1 (and_1_out, ALU_Op[0], ALU_Op[1], not_2_out);
  Adder #(.width(16)) adder_1 (.a(A), .b(multiplexer_1_out), .out(adder_1_out), .cin(and_1_out));  // open: cout
  not not_2 (not_2_out, ALU_Op[2]);
  assign and_2_out = multiplexer_1_out & A;  // AND_Gate and_2, 16 bits wide
  assign or_1_out = multiplexer_1_out | A;  // OR_Gate or_1, 16 bits wide
  Multiplexer #(.select(3), .width(16), .enable("false")) multiplexer_2 (
    .in0(adder_1_out), .in1(and_2_out), .in2(or_1_out), .in3(adder_1_out), .out(ALU_Out), .sel(ALU_Op));  // open: in4, in5, in6, in7
  Comparator #(.width(16), .mode("unsigned")) comparator_1 (.a({16{1'b0}}), .b(ALU_Out), .eq(Zero));  // open: gt, lt

  // Notes on the sheet:
  //   16 Bit ALU
  //   00 = ADD
  //   01 = AND
  //   10 = OR
  //   11 = SUB
  //   sub not B
  //   sub cin
  //   sub
endmodule

module _8x16_bit_Register_File (
  input  [15:0] Data_In,
  input  [3:0] Read_Addr_1,
  input  Write_Enable,
  input  [3:0] Write_Addr,
  input  [3:0] Read_Addr_2,
  input  Clock,
  output [15:0] Read_1_Data,
  output [15:0] Read_2_Data
);

  wire e0, e1, e2, e3, e4, e5, e6, e7, e8, e9, e10, e11, e12, e13, e14, e15;
  wire [15:0] _0, _1, _2, _3, _4, _5, _6, _7, _8, _9, _10, _11, _12, _13, _14, _15;

  Demultiplexer #(.select(4), .enable("false")) demultiplexer_1 (
    .out0(e0), .out1(e1), .out2(e2), .out3(e3), .out4(e4), .out5(e5), .out6(e6), .out7(e7), .out8(e8),
    .out9(e9), .out10(e10), .out11(e11), .out12(e12), .out13(e13), .out14(e14), .out15(e15),
    .in(Write_Enable), .sel(Write_Addr));
  Register #(.width(16)) register_1 (.D(Data_In), .en(1'b0), .Q(_0), .clk(Clock));  // open: clr
  Register #(.width(16)) register_2 (.D(Data_In), .en(e1), .Q(_1), .clk(Clock));  // open: clr
  Register #(.width(16)) register_3 (.D(Data_In), .en(e2), .Q(_2), .clk(Clock));  // open: clr
  Register #(.width(16)) register_4 (.D(Data_In), .en(e3), .Q(_3), .clk(Clock));  // open: clr
  Register #(.width(16)) register_5 (.D(Data_In), .en(e4), .Q(_4), .clk(Clock));  // open: clr
  Register #(.width(16)) register_6 (.D(Data_In), .en(e5), .Q(_5), .clk(Clock));  // open: clr
  Register #(.width(16)) register_7 (.D(Data_In), .en(e6), .Q(_6), .clk(Clock));  // open: clr
  Register #(.width(16)) register_8 (.D(Data_In), .en(e7), .Q(_7), .clk(Clock));  // open: clr
  Register #(.width(16)) register_9 (.D(Data_In), .en(e8), .Q(_8), .clk(Clock));  // open: clr
  Register #(.width(16)) register_10 (.D(Data_In), .en(e9), .Q(_9), .clk(Clock));  // open: clr
  Register #(.width(16)) register_11 (.D(Data_In), .en(e10), .Q(_10), .clk(Clock));  // open: clr
  Register #(.width(16)) register_12 (.D(Data_In), .en(e11), .Q(_11), .clk(Clock));  // open: clr
  Register #(.width(16)) register_13 (.D(Data_In), .en(e12), .Q(_12), .clk(Clock));  // open: clr
  Register #(.width(16)) register_14 (.D(Data_In), .en(e13), .Q(_13), .clk(Clock));  // open: clr
  Register #(.width(16)) register_15 (.D(Data_In), .en(e14), .Q(_14), .clk(Clock));  // open: clr
  Register #(.width(16)) register_16 (.D(Data_In), .en(e15), .Q(_15), .clk(Clock));  // open: clr
  Multiplexer #(.select(4), .width(16), .enable("false")) multiplexer_1 (
    .in0(_0), .in1(_1), .in2(_2), .in3(_3), .in4(_4), .in5(_5), .in6(_6), .in7(_7), .in8(_8), .in9(_9),
    .in10(_10), .in11(_11), .in12(_12), .in13(_13), .in14(_14), .in15(_15), .out(Read_1_Data),
    .sel(Read_Addr_1));
  Multiplexer #(.select(4), .width(16), .enable("false")) multiplexer_2 (
    .in0(_0), .in1(_1), .in2(_2), .in3(_3), .in4(_4), .in5(_5), .in6(_6), .in7(_7), .in8(_8), .in9(_9),
    .in10(_10), .in11(_11), .in12(_12), .in13(_13), .in14(_14), .in15(_15), .out(Read_2_Data),
    .sel(Read_Addr_2));
endmodule

module Control_Logic (
  input  [3:0] Op,
  input  [3:0] Funct,
  output Jump,
  output MemtoReg,
  output MemWrite,
  output Branch,
  output [2:0] ALUControl,
  output ALUSrc,
  output RegDst,
  output RegWrite
);

  wire and_1_out;
  wire [3:1] ram_1_data;

  RAM #(.addrWidth(4), .dataWidth(10)) ram_1 (
    .addr(Op), .data({RegWrite, RegDst, ALUSrc, Branch, MemWrite, MemtoReg, ram_1_data, Jump}));  // open: sel, clk, ld, clr
  and and_1 (and_1_out, ram_1_data[3], ram_1_data[2], ram_1_data[1]);
  Multiplexer #(.width(3), .enable("false")) multiplexer_1 (
    .in0(ram_1_data), .in1(Funct[2:0]), .out(ALUControl), .sel(and_1_out));

  // Notes on the sheet:
  //   Main Decoder
endmodule

module Basic_CPU (
  input  Cloock,
  output [15:0] CPU_Ouput
);

  wire Ctrl_alusrc, Ctrl_memtoreg, Ctrl_memwrite, Ctrl_regdst, Ctrl_regwrite;
  wire [2:0] Ctrl_alucontrol;
  wire [3:0] multiplexer_1_out;
  wire [15:0] adder_1_out, bit_extender_1_out, multiplexer_2_out, multiplexer_3_out, PC_q, ram_2_data,
       RF_read_1_data, RF_read_2_data;
  wire [19:0] ram_1_data;

  Adder #(.width(16)) adder_1 (.a(PC_q), .b(16'h1), .out(adder_1_out));  // open: cin, cout
  Register #(.width(16)) PC (.D(adder_1_out), .Q(PC_q), .clk(Cloock));  // open: en, clr
  RAM #(.addrWidth(16), .dataWidth(20), .bus("separate")) ram_1 (
    .addr(PC_q), .data(ram_1_data), .ld(1'b1));  // open: din, str, sel, clk, clr
  Control_Logic Ctrl (
    .Op(ram_1_data[19:16]), .Funct(ram_1_data[3:0]), .MemtoReg(Ctrl_memtoreg), .MemWrite(Ctrl_memwrite),
    .ALUControl(Ctrl_alucontrol), .ALUSrc(Ctrl_alusrc), .RegDst(Ctrl_regdst), .RegWrite(Ctrl_regwrite));  // open: Jump, Branch
  _8x16_bit_Register_File RF (
    .Data_In(multiplexer_2_out), .Write_Enable(Ctrl_regwrite), .Clock(Cloock),
    .Write_Addr(multiplexer_1_out), .Read_Addr_1(ram_1_data[15:12]), .Read_Addr_2(ram_1_data[11:8]),
    .Read_1_Data(RF_read_1_data), .Read_2_Data(RF_read_2_data));
  Multiplexer #(.width(4), .enable("false")) multiplexer_1 (
    .in0(ram_1_data[11:8]), .in1(ram_1_data[7:4]), .out(multiplexer_1_out), .sel(Ctrl_regdst));
  assign bit_extender_1_out = {{8{ram_1_data[7]}}, ram_1_data[7:0]};  // Bit_Extender bit_extender_1
  Multiplexer #(.width(16), .enable("false")) multiplexer_2 (
    .in0(CPU_Ouput), .in1(ram_2_data), .out(multiplexer_2_out), .sel(Ctrl_memtoreg));
  _16_bit_ALU ALU (
    .A(RF_read_1_data), .B(multiplexer_3_out), .ALU_Op(Ctrl_alucontrol), .ALU_Out(CPU_Ouput));  // open: Zero
  Multiplexer #(.width(16), .enable("false")) multiplexer_3 (
    .in0(RF_read_2_data), .in1(bit_extender_1_out), .out(multiplexer_3_out), .sel(Ctrl_alusrc));
  RAM #(.addrWidth(16), .dataWidth(16), .bus("separate")) ram_2 (
    .addr(CPU_Ouput), .din(RF_read_2_data), .data(ram_2_data), .str(Ctrl_memwrite), .sel(1'b1), .clk(Cloock),
    .ld(1'b1));  // open: clr

  // Other names for the same wires on the sheet: CLK = Cloock

  // Notes on the sheet:
  //   IM
  //   funct: 0-3
  //   rd:    4-7
  //   rt:   8-11
  //   rs: 12-15
  //   op: 16-19
  //   RegDst
  //   MemtoReg
  //   ALUSrc
  //   DM
endmodule
